# Fritzing sketch ArduTemperatureMonitor (saved by Fritzing 0.8.3b)
breadboards: 1

parts:
  U1 = Arduino Uno (Rev3)
  R1 = Resistor [tolerance=±5% resistance=220 package=THT]
  U2 = TMP36 [part_number=TMP36 package=to-92-kit]
  C1 = Ceramic Capacitor [capacitance=0.1µF voltage=16V package="100 mil [THT, multilayer]"]
  R2 = Trimmer Potentiometer [maximum_resistance=10kΩ package=THT]
  LCD_Display = LCD-16X2 [part_number=HD44780 package=lcd-16x2]

nets:
  N1: U1.A0, U2.VOUT
  GND: U1.GND, U2.GND, C1.0, R2.leg2, LCD_Display.VSS, LCD_Display.R_W, LCD_Display.K
  N2: U1.D11_PWM/MOSI, LCD_Display.E
  N3: U1.D12/MISO, LCD_Display.RS
  N4: U1.D2, LCD_Display.DB7
  N5: U1.D3_PWM, LCD_Display.DB6
  N6: U1.D4, LCD_Display.DB5
  N7: U1.D5_PWM, LCD_Display.DB4
  5V: U1.5V, R1.Pin_0, U2.VCC, C1.1, R2.leg1, LCD_Display.VDD
  N8: R1.Pin_1, LCD_Display.A
  N9: R2.wiper, LCD_Display.VO
